# Fritzing sketch Smart_Room_Fritzing (saved by Fritzing 1.0.0rc)
breadboards: 1

parts:
  A1 = Particle - Photon2
  Neopixel1 = Adafruit RBG Smart Neopixel [package="DIP (Dual Inline) [THT]"]
  Neopixel2 = Adafruit RBG Smart Neopixel [package="DIP (Dual Inline) [THT]"]
  Neopixel3 = Adafruit RBG Smart Neopixel [package="DIP (Dual Inline) [THT]"]
  M1 = Dagu DGServo 9g (Top view) [part_number=RS001B]
  M2 = Dagu DGServo 9g (Top view) [part_number=RS001B]
  P1 = S1133 Si Photodiode [package="8mm Ceramic [THT]"]
  R1 = Resistor [tolerance=±5% resistance=220 package="2512 [SMD]"]
  Rain_Sensor = Water Level Sensor
  Stand_In_for_Motion_Sensor = Water Level Sensor
  S1 = Pushbutton [package="[THT]"]
  S2 = Pushbutton [package="[THT]"]

nets:
  VCC: A1.Pin_2, M1.vcc, M2.vcc, P1.anode, Rain_Sensor.VCC, Stand_In_for_Motion_Sensor.VCC, S1.Pin_3, S1.Pin_4, S2.Pin_3
  GND: A1.Pin_4, A1.Pin_30, Neopixel1.G, Neopixel2.G, Neopixel3.G, M1.gnd, M2.gnd, R1.Pin_1, Rain_Sensor.GND, Stand_In_for_Motion_Sensor.GND
  N1: A1.Pin_7, M1.pulse, M2.pulse
  N2: A1.Pin_8, P1.cathode, R1.Pin_0
  N3: A1.Pin_12, Rain_Sensor.SIG
  N4: A1.Pin_13, Stand_In_for_Motion_Sensor.SIG
  N5: A1.Pin_14, S1.Pin_1, S1.Pin_2
  N6: A1.Pin_15, S2.Pin_1, S2.Pin_2
  N7: A1.Pin_19, Neopixel1.In
  N8: A1.Pin_26, Neopixel1.+, Neopixel2.+, Neopixel3.+
  N9: Neopixel1.O, Neopixel2.In
  N10: Neopixel2.O, Neopixel3.In

custom parts:
  Particle - Photon2: The Photon 2 is a microcontroller and Wi-Fi networking developed by particle. Features: 802.11a/b/g/n Wi-Fi, 2.4 GHz and 5 GHz Integrated PCB antenna Integrated U.FL connector for external antenna Integrated RF switch BLE 5 using same antenna as Wi-Fi Realtek RTL8721DM MCU ARM Cortex M33 CPU, 200 MHz 2048 KB (2 MB) user application maximum size 3072 KB (3 MB) of RAM available to user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
  Water Level Sensor: A water level sensor. This sensor operates at 3V to 5V. The Sig (signal) pin outputs an analogue signal that is in proportion to the amount of water in contact with the sensor.
  Pushbutton: A generic pushbutton.
